# Fritzing sketch the circuit on stripbord (saved by Fritzing 0.9.3b)
stripboards: 1

parts:
  MAX1 = Mystery Part - 8 pins [chip_label=MAX485 package=THT]
  Part1 = Arduino Nano (Rev3.0)
  RHT1 = Humidity and Temperature Sensor RHT03

nets:
  N1: MAX1.RO, Part1.D0/RX
  N2: MAX1.RE, MAX1.DE, Part1.D2
  N3: MAX1.DO, Part1.D1/TX
  GND: MAX1.GND, Part1.GND, RHT1.GND_2
  VCC: MAX1.VCC, Part1.5V, RHT1.Vcc
  N4: Part1.D7, RHT1.Data-signal

notes:
  R = 1.2K not 1K

custom parts:
  Mystery Part - 8 pins: A dummy, proxy, ersatz, stand-in part for whatever you want. With 8 pins on a 900mil inline pin header footprint.
